# Fritzing sketch esquema (saved by Fritzing 0.9.3b)
breadboards: 1

parts:
  Componente1 = DeuLigne 1.1 - The Snootlab's LCD shield for Arduino
  Componente2 = Arduino Uno (Rev3)
  R1 = Photocell (LDR) [package=THT]
  RHT1 = Humidity and Temperature Sensor RHT03
  U2 = RELAY [package=relay-g5q]
  R2 = Resistor [tolerance=±5% resistance=1k package="1206 [SMD]"]
  J1 = Peltier Element
  J2 = Power Jack [package=power_jack_slot]

nets:
  N1: Componente1.A0, Componente2.A0
  N2: Componente1.A1, Componente2.A1
  N3: Componente1.A2, Componente2.A2
  N4: Componente1.A3, Componente2.A3
  N5: Componente1.A4(SDA), Componente2.A4/SDA
  N6: Componente1.A5(CLK), Componente2.A5/SCL, R1.pin_1, R2.Pin_1
  N7: Componente1.D2, Componente2.D2, RHT1.Data-signal
  N8: Componente1.D3, Componente2.D3_PWM, U2.COIL2
  +5V: Componente1.+5V, Componente2.5V, R1.pin_0, RHT1.Vcc
  GND: Componente1.GND, Componente2.GND, RHT1.GND_2, U2.COIL1, R2.Pin_0
  N9: Componente1.D8, Componente2.D8
  N10: Componente1.D9, Componente2.D9_PWM
  N11: Componente1.D10_SS, Componente2.D10_PWM/SS
  N12: Componente1.D11_MOSI, Componente2.D11_PWM/MOSI
  N13: Componente1.D12_MISO, Componente2.D12/MISO
  N14: Componente1.D13_SCK, Componente2.D13/SCK
  N15: Componente1.AREF, Componente2.AREF
  N16: Componente1.D0_RX, Componente2.D0/RX
  N17: Componente1.D1_TX, Componente2.D1/TX
  N18: Componente1.D4, Componente2.D4
  N19: Componente1.D5, Componente2.D5_PWM
  N20: Componente1.D6, Componente2.D6_PWM
  N21: Componente1.D7, Componente2.D7
  N22: Componente1.RESET, Componente2.RESET
  +3V3: Componente1.+3V3, Componente2.3V3
  VIN: Componente1.VIN, Componente2.VIN
  N23: U2.MAIN, J1.pin2
  N24: U2.NO, J2.PWR
  N25: J1.pin1, J2.GND

notes:
  componentes necessários:
  -arduino
  -LCD Keypad Shield
  -DHT11
  -relay
  -ldr
  -resistor 1kΩ
  -power jack(ou qualquer fonte de energia de 5v ou voltagem recomendada para alimentação do peltier)
  -peltier
  /!\ obs: use um lcd keypad Shield com encaixe compativel com o arduino escolhido, a imagem da conexão do keypad shield no arduino é apenas uma ilustração!!!!
